# Fritzing sketch Fritzing Sketch Source File (saved by Fritzing 0.9.3b)
breadboards: 1

parts:
  Part1 = Arduino Uno (Rev3)
  LED1 = LED - 5mm [color="Red (633nm)" package="5 mm [THT]"]
  LED2 = LED - 5mm [color="Red (633nm)" package="5 mm [THT]"]
  R1 = Resistor [tolerance=±5% resistance=220 package="0805 [SMD]"]
  R2 = Resistor [tolerance=±5% resistance=220 package="0805 [SMD]"]
  BAT1 = BC9VPC [package=bc9vpc]
  J1 = Piezo Speaker
  U2 = SWITCH-SPST-2 [package=switch-spst-vertical]
  Part2 = HC-SR501 Body Sensor Module

nets:
  N1: Part1.D9_PWM, R1.Pin_0
  N2: Part1.D11_PWM/MOSI, R2.Pin_1
  N3: Part1.D13/SCK, J1.pin2
  N4: Part1.GND, J1.pin1
  N5: Part1.D3_PWM, Part2.OUT
  N6: LED1.cathode, LED2.cathode, BAT1.V-, Part2.GND
  N7: LED1.anode, R2.Pin_0
  N8: LED2.anode, R1.Pin_1
  N9: BAT1.V+, U2.O

notes:
  GND - Black Wire
  5VC - Red Wire
  GPIO - Blue Or Grey Wire
  Intruder Alarm System Using PIR Motion Sensor
  ---- Graphical Diagram ----
  Intruder Alarm System Using PIR Motion Sensor
  ---- Circuit Diagram ----

custom parts:
  HC-SR501 Body Sensor Module: Pyroelectric Infrared PIR Motion Sensor Detector Module
